# Fritzing sketch pinball (saved by Fritzing 0.8.7b)
breadboards: 1

parts:
  Flipper1 = DC Motor
  Flipper2 = DC Motor
  Motor_Driver = L298_BRIDGE_DRIVER [package=powerso20]
  U1 = ESP32S-HiLetgo [part_number=ESP32S-HiLetgo]
  Power_Arduino = Power plug
  Power_motor = Power plug
  Limit_switch1 = SWITCH-MOMENTARY-2 [package=tactile_switch_smd-2]
  Limit_switch2 = SWITCH-MOMENTARY-2 [package=tactile_switch_smd-2]
  Limit_switch3 = SWITCH-MOMENTARY-2 [package=tactile_switch_smd-2]
  Limit_switch4 = SWITCH-MOMENTARY-2 [package=tactile_switch_smd-2]
  R1 = Resistor [package="2010 [SMD]"]
  Vibration_sensor = Piezo Speaker
  R2 = Resistor [package="2010 [SMD]"]

nets:
  N1: Flipper1.pin_1, Motor_Driver.OUT2
  N2: Flipper1.pin_2, Motor_Driver.OUT1
  N3: Flipper2.pin_1, Motor_Driver.OUT4
  N4: Flipper2.pin_2, Motor_Driver.OUT3
  GND: Motor_Driver.GND, U1.GND, Power_Arduino.GND, Power_motor.GND, Limit_switch1.2, Limit_switch2.2, Limit_switch3.2, Limit_switch4.2, Vibration_sensor.pin1, R2.Pin_1
  N5: Motor_Driver.VS, Power_motor.VCC
  N6: Motor_Driver.IN1, U1.GPIO17
  N7: Motor_Driver.ENA, U1.GPIO16
  N8: Motor_Driver.IN2, U1.GPIO4
  VSS: Motor_Driver.VSS, U1.VIN, Power_Arduino.VCC, R1.Pin_0
  N9: Motor_Driver.IN3, U1.GPIO15
  N10: Motor_Driver.ENB, U1.GPIO2
  N11: Motor_Driver.IN4, U1.GPIO0
  N12: U1.GPIO36, Vibration_sensor.pin2, R2.Pin_0
  N13: U1.GPIO26, U1.GPIO27, U1.GPIO14, U1.GPIO12, Limit_switch1.1, Limit_switch2.1, Limit_switch3.1, Limit_switch4.1, R1.Pin_1

custom parts:
  ESP32S-HiLetgo: HiLetgo ESP-WROOM-32 ESP32 ESP-32S Development Board 2.4GHz Dual-Mode WiFi + Bluetooth Dual Cores Microcontroller The ESP32 integrated with Antenna switches, RF Balun, power amplifiers, low-noise amplifiers, filters, and management modules, and the entire solution occupies the least area of PCB. 2.4 GHz Wi-Fi plus Bluetooth dual-mode chip, with TSMC Ultra-low power consumption 40nm technology,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
